# Fritzing sketch schematic (saved by Fritzing 0.9.6b)
breadboards: 1

parts:
  Part1 = ACS712 Current Sensor 5A 20A 30A
  MH-ET_Live_Minikit_for_ESP1 = MH-ET Live Minikit for ESP32

nets:
  VCC: Part1.VCC, MH-ET_Live_Minikit_for_ESP1.VCC, MH-ET_Live_Minikit_for_ESP1.SD0
  N1: Part1.OUT, MH-ET_Live_Minikit_for_ESP1.SVP
  GND: Part1.GND, MH-ET_Live_Minikit_for_ESP1.GND

custom parts:
  ACS712 Current Sensor 5A 20A 30A: Remix by Michael Kubina http://www.kubina.info Original by: https://forum.fritzing.org/t/current-sensor-5a-acs712/7694 https://forum.fritzing.org/u/ArtHome ArtHome12@gmail.com
  MH-ET Live Minikit for ESP32: MH-ET Live Minikit for ESP32 ( http://mh.nodebb.com/topic/8/mh-et-live-minikit-for-esp32/2/) PCB footprint is invalid.
